# Fritzing sketch ArduinoPDM_v1.0.3 (saved by Fritzing 0.9.10b)
circuit board: 9cm x 5cm
breadboards: 1

parts:
  MCP2515 = Niren can bus module [package=THT]
  Arduino = Arduino Nano (Rev3.0)
  8_Channel_Relay = 8 Channel Power Relay

nets:
  5V: MCP2515.pin1, Arduino.5V, 8_Channel_Relay.VCC
  GND: MCP2515.pin2, Arduino.GND, 8_Channel_Relay.GND
  N1: MCP2515.pin3, Arduino.D10
  N2: MCP2515.pin4, Arduino.D12/MISO
  N3: MCP2515.pin5, Arduino.D11/MOSI
  N4: MCP2515.pin6, Arduino.D13/SCK
  N5: MCP2515.pin7, Arduino.D2
  N6: Arduino.D3, 8_Channel_Relay.IN7
  N7: Arduino.D4, 8_Channel_Relay.IN6
  N8: Arduino.D5, 8_Channel_Relay.IN5
  N9: Arduino.D6, 8_Channel_Relay.IN4
  N10: Arduino.D7, 8_Channel_Relay.IN3
  N11: Arduino.D8, 8_Channel_Relay.IN2
  N12: Arduino.D9, 8_Channel_Relay.IN1
  N13: Arduino.A0, 8_Channel_Relay.IN8

notes:
  ArduinoPDM v1.0.3
  ErRoR Engineering
  D13
  TX1
  USB

custom parts:
  Niren can bus module: Niren can bus module availabe on ebay and others. Pcb view assumes that you unsolder the 7 pin header and resolder it on the bottom of the module to connect to the pcb. The two jumpers and the can bus connector remain on the top of the board and don't appear in pcb view.
  8 Channel Power Relay: An 8 channel power relay. The module operates at 5V.
